# Fritzing sketch Retrostick (saved by Fritzing 0.9.3b)
circuit board: 6.61567cm x 5.87531cm
breadboards: 1

parts:
  Rb1 = Resistor [tolerance=±5% resistance=1k package=THT]
  Rb2 = Resistor [tolerance=±5% resistance=1k package=THT]
  Rc2 = Resistor [tolerance=±5% resistance=2.2k package=THT]
  Rb4 = Resistor [tolerance=±5% resistance=1k package=THT]
  Rb3 = Resistor [tolerance=±5% resistance=1k package=THT]
  Rc4 = Resistor [tolerance=±5% resistance=2.2k package=THT]
  Rc3 = Resistor [tolerance=±5% resistance=2.2k package=THT]
  Rb6 = Resistor [tolerance=±5% resistance=1k package=THT]
  Rb5 = Resistor [tolerance=±5% resistance=1k package=THT]
  Rc6 = Resistor [tolerance=±5% resistance=2.2k package=THT]
  Rc5 = Resistor [tolerance=±5% resistance=2.2k package=THT]
  J1 = female pin header, 7 pins [form="♀ (female)"]
  J2 = female pin header, 7 pins [form="♀ (female)"]
  Q3 = NPN-Transistor [package="TO92 [THT]"]
  Q4 = NPN-Transistor [package="TO92 [THT]"]
  Q6 = NPN-Transistor [package="TO92 [THT]"]
  Rc1 = Resistor [tolerance=±5% resistance=2.2k package=THT]
  Q5 = NPN-Transistor [package="TO92 [THT]"]
  Q2 = NPN-Transistor [package="TO92 [THT]"]
  Q1 = NPN-Transistor [package="TO92 [THT]"]

nets:
  N1: Rb1.Pin_0, J2.pin7
  N2: Rb1.Pin_1, Q1.B
  N3: Rb2.Pin_0, J2.pin6
  N4: Rb2.Pin_1, Q2.B
  N5: Rc2.Pin_0, Q2.C
  N6: Rc2.Pin_1, J1.pin2
  N7: Rb4.Pin_0, J2.pin4
  N8: Rb4.Pin_1, Q4.B
  N9: Rb3.Pin_0, J2.pin5
  N10: Rb3.Pin_1, Q3.B
  N11: Rc4.Pin_0, Q4.C
  N12: Rc4.Pin_1, J1.pin4
  N13: Rc3.Pin_0, Q3.C
  N14: Rc3.Pin_1, J1.pin3
  N15: Rb6.Pin_0, J2.pin2
  N16: Rb6.Pin_1, Q6.B
  N17: Rb5.Pin_0, J2.pin3
  N18: Rb5.Pin_1, Q5.B
  N19: Rc6.Pin_0, Q6.C
  N20: Rc6.Pin_1, J1.pin6
  N21: Rc5.Pin_0, Q5.C
  N22: Rc5.Pin_1, J1.pin5
  N23: J1.pin1, Rc1.Pin_1
  N24: J1.pin7, J2.pin1, Q3.E, Q4.E, Q6.E, Q5.E, Q2.E, Q1.E
  N25: Rc1.Pin_0, Q1.C
